# Fritzing sketch Sonar1 (saved by Fritzing 0.9.10b)
breadboards: 1

parts:
  HC-SR04_Sensor_1 = HC-SR04 Ultrasonic Distance Sensor
  부품2 = Arduino Due (Rev2b)

nets:
  VCC: HC-SR04_Sensor_1.VCC, 부품2.5V
  N1: HC-SR04_Sensor_1.TRIG, 부품2.D22
  N2: HC-SR04_Sensor_1.ECHO, 부품2.D23
  GND: HC-SR04_Sensor_1.GND, 부품2.GND
