# Fritzing sketch Sonar3 (saved by Fritzing 0.9.10b)
breadboards: 1

parts:
  HC-SR04_Sensor_1 = HC-SR04 Ultrasonic Distance Sensor
  부품2 = Arduino Due (Rev2b)
  S1 = H-Bridge with L298N  # not connected
  HC-SR04_Sensor_2 = HC-SR04 Ultrasonic Distance Sensor
  HC-SR04_Sensor_3 = HC-SR04 Ultrasonic Distance Sensor

nets:
  VCC: HC-SR04_Sensor_1.VCC, 부품2.5V, HC-SR04_Sensor_2.VCC, HC-SR04_Sensor_3.VCC
  N1: HC-SR04_Sensor_1.TRIG, 부품2.D3_PWM
  N2: HC-SR04_Sensor_1.ECHO, 부품2.D4_PWM/SS1
  GND: HC-SR04_Sensor_1.GND, 부품2.GND, HC-SR04_Sensor_2.GND, HC-SR04_Sensor_3.GND
  N3: 부품2.D8_PWM, HC-SR04_Sensor_3.TRIG
  N4: 부품2.D9_PWM, HC-SR04_Sensor_3.ECHO
  N5: 부품2.D5_PWM, HC-SR04_Sensor_2.TRIG
  N6: 부품2.D6_PWM, HC-SR04_Sensor_2.ECHO

custom parts:
  H-Bridge with L298N: h-bridge
